// Logisim project ex4.circ as structural Verilog: 5 circuits, main circuit RotRight
module RotRight (
  input  [15:0] INPUT0,
  input  [3:0] AMOUNT,
  output [15:0] OUTPUT0
);

  wire [15:0] and_1_out, and_2_out, and_3_out, and_4_out, and_5_out, and_6_out, and_7_out, and_8_out,
       bit_extender_1_out, bit_extender_2_out, bit_extender_3_out, bit_extender_4_out, D1, D2, D3, not_1_out,
       not_2_out, not_3_out, not_4_out, rot1_1_out_2, rot2_1_out_2, rot4_1_out_2, rot8_1_out_2;

  assign bit_extender_1_out = {{15{AMOUNT[0]}}, AMOUNT[0]};  // Bit_Extender bit_extender_1
  assign bit_extender_2_out = {{15{AMOUNT[1]}}, AMOUNT[1]};  // Bit_Extender bit_extender_2
  assign bit_extender_3_out = {{15{AMOUNT[2]}}, AMOUNT[2]};  // Bit_Extender bit_extender_3
  assign bit_extender_4_out = {{15{AMOUNT[3]}}, AMOUNT[3]};  // Bit_Extender bit_extender_4
  rot1 rot1_1 (.in_1(INPUT0), .out_2(rot1_1_out_2));
  assign not_1_out = ~bit_extender_1_out;  // NOT_Gate not_1, 16 bits wide
  rot2 rot2_1 (.in_1(D1), .out_2(rot2_1_out_2));
  assign not_2_out = ~bit_extender_2_out;  // NOT_Gate not_2, 16 bits wide
  rot4 rot4_1 (.in_1(D2), .out_2(rot4_1_out_2));
  assign not_3_out = ~bit_extender_3_out;  // NOT_Gate not_3, 16 bits wide
  rot8 rot8_1 (.in_1(D3), .out_2(rot8_1_out_2));
  assign not_4_out = ~bit_extender_4_out;  // NOT_Gate not_4, 16 bits wide
  assign and_1_out = bit_extender_1_out & rot1_1_out_2;  // AND_Gate and_1, 16 bits wide
  assign and_2_out = not_1_out & INPUT0;  // AND_Gate and_2, 16 bits wide
  assign and_3_out = bit_extender_2_out & rot2_1_out_2;  // AND_Gate and_3, 16 bits wide
  assign and_4_out = not_2_out & D1;  // AND_Gate and_4, 16 bits wide
  assign and_5_out = bit_extender_3_out & rot4_1_out_2;  // AND_Gate and_5, 16 bits wide
  assign and_6_out = not_3_out & D2;  // AND_Gate and_6, 16 bits wide
  assign and_7_out = bit_extender_4_out & rot8_1_out_2;  // AND_Gate and_7, 16 bits wide
  assign and_8_out = not_4_out & D3;  // AND_Gate and_8, 16 bits wide
  assign D1 = and_1_out | and_2_out;  // OR_Gate or_1, 16 bits wide
  assign D2 = and_3_out | and_4_out;  // OR_Gate or_2, 16 bits wide
  assign D3 = and_5_out | and_6_out;  // OR_Gate or_3, 16 bits wide
  assign OUTPUT0 = and_7_out | and_8_out;  // OR_Gate or_4, 16 bits wide

  // Other names for the same wires on the sheet: D0[15:0] = INPUT0
endmodule

module rot1 (
  input  [15:0] in_1,
  output [15:0] out_2
);


  assign out_2 = {in_1[0], in_1[15:1]};
endmodule

module rot2 (
  input  [15:0] in_1,
  output [15:0] out_2
);


  assign out_2 = {in_1[1:0], in_1[15:2]};
endmodule

module rot4 (
  input  [15:0] in_1,
  output [15:0] out_2
);


  assign out_2 = {in_1[3:0], in_1[15:4]};
endmodule

module rot8 (
  input  [15:0] in_1,
  output [15:0] out_2
);


  assign out_2 = {in_1[7:0], in_1[15:8]};
endmodule
