// Logisim project control-logic.circ as structural Verilog: 1 circuit, main circuit control_logic
module control_logic (
  input  [31:0] Instruction,
  input  BrEq,
  input  BrLt,
  output PCSel,
  output RegWEn,
  output [2:0] ImmSel,
  output BrUn,
  output ASel,
  output BSel,
  output [3:0] ALUSel,
  output MemWEn,
  output [1:0] WBSel
);

  wire and_1_out, and_2_out, and_3_out, and_4_out, comparator_2_eq, comparator_3_eq, comparator_4_eq,
       comparator_5_eq, comparator_6_eq, comparator_7_eq, comparator_8_eq, comparator_9_eq, comparator_10_eq,
       comparator_11_eq, comparator_12_eq, comparator_13_eq, comparator_14_eq, comparator_16_eq,
       comparator_17_eq, comparator_18_eq, comparator_19_eq, comparator_20_eq, comparator_21_eq,
       comparator_22_eq, comparator_23_eq, comparator_24_eq, comparator_25_eq, comparator_26_eq,
       comparator_27_eq, comparator_28_eq, comparator_29_eq, comparator_30_eq, comparator_31_eq,
       comparator_32_eq, comparator_33_eq, comparator_34_eq, multiplexer_11_out, not_1_out, not_2_out,
       not_3_out, not_4_out, or_1_out, or_2_out, or_5_out, or_6_out, or_7_out, or_8_out, or_9_out;
  wire [3:0] ALUSel_T, bit_extender_1_out, bit_extender_2_out, multiplexer_1_out, multiplexer_2_out,
       multiplexer_3_out, multiplexer_4_out, multiplexer_5_out, multiplexer_6_out, multiplexer_7_out,
       multiplexer_8_out, multiplexer_9_out;

  Comparator #(.width(7)) comparator_1 (.a(Instruction[6:0]), .b(7'b0110011), .eq(BSel));  // open: gt, lt
  Comparator #(.width(7)) comparator_2 (.a(Instruction[6:0]), .b(7'b0110111), .eq(comparator_2_eq));  // open: gt, lt
  Comparator #(.width(7)) comparator_3 (.a(Instruction[6:0]), .b(7'b0010111), .eq(comparator_3_eq));  // open: gt, lt
  Comparator #(.width(7)) comparator_4 (.a(Instruction[6:0]), .b(7'b0010011), .eq(comparator_4_eq));  // open: gt, lt
  Comparator #(.width(7)) comparator_5 (.a(Instruction[6:0]), .b(7'b0000011), .eq(comparator_5_eq));  // open: gt, lt
  Comparator #(.width(7)) comparator_6 (.a(Instruction[6:0]), .b(7'b1101111), .eq(comparator_6_eq));  // open: gt, lt
  Comparator #(.width(7)) comparator_7 (.a(Instruction[6:0]), .b(7'b1100111), .eq(comparator_7_eq));  // open: gt, lt
  Comparator #(.width(7)) comparator_8 (.a(Instruction[6:0]), .b(7'b0010011), .eq(comparator_8_eq));  // open: gt, lt
  Comparator #(.width(7)) comparator_9 (.a(Instruction[6:0]), .b(7'b1100111), .eq(comparator_9_eq));  // open: gt, lt
  Comparator #(.width(7)) comparator_10 (.a(Instruction[6:0]), .b(7'b0000011), .eq(comparator_10_eq));  // open: gt, lt
  Comparator #(.width(7)) comparator_11 (.a(Instruction[6:0]), .b(7'b1101111), .eq(comparator_11_eq));  // open: gt, lt
  Comparator #(.width(7)) comparator_12 (.a(Instruction[6:0]), .b(7'b1100011), .eq(comparator_12_eq));  // open: gt, lt
  Comparator #(.width(7)) comparator_13 (.a(Instruction[6:0]), .b(7'b0010111), .eq(comparator_13_eq));  // open: gt, lt
  Comparator #(.width(7)) comparator_14 (.a(Instruction[6:0]), .b(7'b0110111), .eq(comparator_14_eq));  // open: gt, lt
  Comparator #(.width(7)) comparator_15 (.a(Instruction[6:0]), .b(7'b0100011), .eq(MemWEn));  // open: gt, lt
  Comparator #(.width(7)) comparator_16 (.a(Instruction[6:0]), .b(7'b1101111), .eq(comparator_16_eq));  // open: gt, lt
  or or_1 (or_1_out, comparator_8_eq, comparator_9_eq, comparator_10_eq);
  or or_2 (or_2_out, comparator_13_eq, comparator_14_eq);
  not not_1 (not_1_out, comparator_10_eq);
  and and_1 (and_1_out, not_1_out, not_2_out);
  not not_2 (not_2_out, comparator_16_eq);
  or or_3 (RegWEn, BSel, comparator_2_eq, comparator_3_eq, comparator_4_eq, comparator_5_eq, comparator_6_eq, comparator_7_eq);
  Priority_Encoder priority_encoder_1 (
    .in0(or_1_out), .in1(MemWEn), .in2(comparator_12_eq), .in3(or_2_out), .in4(comparator_11_eq), .out(ImmSel));  // open: in5, in6, in7, en_in, gs, en_out
  Priority_Encoder #(.select_enc(2)) priority_encoder_2 (
    .in0(comparator_10_eq), .in1(and_1_out), .in2(comparator_16_eq), .out(WBSel));  // open: in3, gs, en_out, en_in
  Comparator #(.width(7)) comparator_17 (
    .a(Instruction[31:25]), .b(7'b0100000), .eq(comparator_17_eq));  // open: gt, lt
  Comparator #(.width(3)) comparator_18 (.a(Instruction[14:12]), .b(3'b000), .eq(comparator_18_eq));  // open: gt, lt
  Comparator #(.width(3)) comparator_19 (.a(Instruction[14:12]), .b(3'b101), .eq(comparator_19_eq));  // open: gt, lt
  Comparator #(.width(3)) comparator_20 (.a(Instruction[14:12]), .b(3'b001), .eq(comparator_20_eq));  // open: gt, lt
  Comparator #(.width(3)) comparator_21 (.a(Instruction[14:12]), .b(3'b011), .eq(comparator_21_eq));  // open: gt, lt
  assign bit_extender_1_out = {{1{1'b0}}, Instruction[14:12]};  // Bit_Extender bit_extender_1
  Multiplexer #(.width(4)) multiplexer_1 (
    .in0(bit_extender_1_out), .in1(multiplexer_2_out), .out(multiplexer_1_out), .sel(comparator_19_eq));
  Multiplexer #(.width(4)) multiplexer_2 (
    .in0(4'b0101), .in1(4'b1101), .out(multiplexer_2_out), .sel(comparator_17_eq));
  Comparator #(.width(3)) comparator_22 (.a(Instruction[14:12]), .b(3'b110), .eq(comparator_22_eq));  // open: gt, lt
  Comparator #(.width(3)) comparator_23 (.a(Instruction[14:12]), .b(3'b111), .eq(comparator_23_eq));  // open: gt, lt
  Multiplexer #(.width(4)) multiplexer_3 (
    .in0(4'b1101), .in1(4'b1100), .out(multiplexer_3_out), .sel(comparator_18_eq));
  Multiplexer #(.width(4)) multiplexer_4 (
    .in0(4'b1000), .in1(4'b1001), .out(multiplexer_4_out), .sel(comparator_20_eq));
  or or_4 (BrUn, comparator_22_eq, comparator_23_eq);
  Comparator #(.width(7)) comparator_24 (
    .a(Instruction[31:25]), .b(7'b0100000), .eq(comparator_24_eq));  // open: gt, lt
  Comparator #(.width(7)) comparator_25 (
    .a(Instruction[31:25]), .b(7'b0000001), .eq(comparator_25_eq));  // open: gt, lt
  assign bit_extender_2_out = {{1{1'b0}}, Instruction[14:12]};  // Bit_Extender bit_extender_2
  Multiplexer #(.width(4)) multiplexer_5 (
    .in0(multiplexer_4_out), .in1(4'b1011), .out(multiplexer_5_out), .sel(comparator_21_eq));
  or or_5 (or_5_out, comparator_18_eq, comparator_19_eq);
  or or_6 (or_6_out, comparator_18_eq, comparator_20_eq, comparator_21_eq);
  and and_2 (and_2_out, comparator_24_eq, or_5_out);
  Multiplexer #(.width(4)) multiplexer_6 (
    .in0(bit_extender_2_out), .in1(multiplexer_3_out), .out(multiplexer_6_out), .sel(and_2_out));
  Multiplexer #(.width(4)) multiplexer_7 (
    .in0(multiplexer_6_out), .in1(multiplexer_5_out), .out(multiplexer_7_out), .sel(and_3_out));
  and and_3 (and_3_out, comparator_25_eq, or_6_out);
  Multiplexer #(.width(4)) multiplexer_8 (
    .in0(multiplexer_7_out), .in1(multiplexer_1_out), .out(multiplexer_8_out), .sel(comparator_26_eq));
  Multiplexer #(.width(4)) multiplexer_9 (
    .in0(multiplexer_8_out), .in1(4'b1111), .out(multiplexer_9_out), .sel(or_7_out));
  Comparator #(.width(7)) comparator_26 (.a(Instruction[6:0]), .b(7'b0010011), .eq(comparator_26_eq));  // open: gt, lt
  Comparator #(.width(7)) comparator_27 (.a(Instruction[6:0]), .b(7'b0010111), .eq(comparator_27_eq));  // open: gt, lt
  Comparator #(.width(7)) comparator_28 (.a(Instruction[6:0]), .b(7'b0110111), .eq(comparator_28_eq));  // open: gt, lt
  Comparator #(.width(7)) comparator_29 (.a(Instruction[6:0]), .b(7'b0100011), .eq(comparator_29_eq));  // open: gt, lt
  Comparator #(.width(7)) comparator_30 (.a(Instruction[6:0]), .b(7'b0000011), .eq(comparator_30_eq));  // open: gt, lt
  Multiplexer #(.width(4)) multiplexer_10 (.in0(multiplexer_9_out), .in1(4'b0000), .out(ALUSel_T), .sel(or_8_out));
  or or_7 (or_7_out, comparator_27_eq, comparator_28_eq);
  or or_8 (or_8_out, comparator_29_eq, comparator_30_eq);
  not not_3 (not_3_out, BrEq);
  not not_4 (not_4_out, BrLt);
  Multiplexer #(.select(3)) multiplexer_11 (
    .in0(BrEq), .in1(not_3_out), .in4(BrLt), .in5(not_4_out), .in6(BrLt), .in7(not_4_out),
    .out(multiplexer_11_out), .sel(Instruction[14:12]));  // open: in2, in3
  Comparator #(.width(7)) comparator_31 (.a(Instruction[6:0]), .b(7'b1100011), .eq(comparator_31_eq));  // open: gt, lt
  Comparator #(.width(7)) comparator_32 (.a(Instruction[6:0]), .b(7'b0010111), .eq(comparator_32_eq));  // open: gt, lt
  Comparator #(.width(7)) comparator_33 (.a(Instruction[6:0]), .b(7'b1100111), .eq(comparator_33_eq));  // open: gt, lt
  Comparator #(.width(7)) comparator_34 (.a(Instruction[6:0]), .b(7'b1101111), .eq(comparator_34_eq));  // open: gt, lt
  and and_4 (and_4_out, multiplexer_11_out, comparator_31_eq);
  or or_9 (or_9_out, comparator_34_eq, comparator_33_eq, and_4_out, comparator_32_eq);
  Multiplexer #(.width(4)) multiplexer_12 (.in0(ALUSel_T), .in1(4'b0000), .out(ALUSel), .sel(or_9_out));
  or or_10 (PCSel, and_4_out, comparator_33_eq, comparator_34_eq);
  nor nor_1 (ASel, and_4_out, comparator_32_eq, comparator_34_eq);

  // Other names for the same wires on the sheet: opcode[6:0] = Instruction[6:0]; funct3[2:0] = Instruction[14:12];
  //   funct7[6:0] = Instruction[31:25]

  // Notes on the sheet:
  //   INPUTS to your circuit
  //   DON'T CHANGE THE LOCATIONS OF THE INPUTS AND OUTPUTS!
  //   OUTPUT from your circuit
endmodule
