// Logisim project cpu.circ as structural Verilog: 1 circuit, main circuit cpu
module cpu (
  input  clk,
  input  [31:0] Instruction,
  input  [31:0] MemReadData,
  output [31:0] MemAddress,
  output [31:0] ProgramCounter,
  output [31:0] ra,
  output [31:0] sp,
  output [31:0] t0,
  output [31:0] t1,
  output [31:0] t2,
  output [31:0] s0,
  output [31:0] s1,
  output [31:0] a0,
  output [3:0] MemWriteMask,
  output [31:0] MemWriteData
);

  wire ASel, BrEq, BrLt, BrUn, BSel, MemRW, PCSel, RegWEn;
  wire [1:0] WBSel;
  wire [2:0] func3, ImmSel;
  wire [3:0] ALUSel;
  wire [6:0] func7;
  wire [24:0] Instruction_S1;
  wire [31:0] DataToReg, IMM, multiplexer_1_out, multiplexer_2_out, multiplexer_3_out, multiplexer_4_out,
       PC_S1, PCplus4, PCplus4_S1, RegData1, RegData2, WriteBack;

  Adder #(.width(32)) adder_1 (.a(ProgramCounter), .b(32'h4), .out(PCplus4));  // open: cin, cout
  Register #(.width(32)) PC (.D(multiplexer_1_out), .clk(clk), .Q(ProgramCounter));  // open: en, clr
  Multiplexer #(.width(32)) multiplexer_1 (.in0(PCplus4), .in1(MemAddress), .out(multiplexer_1_out), .sel(PCSel));
  Register #(.width(32)) register_1 (
    .D(multiplexer_2_out), .clk(clk), .Q({func7, Instruction_S1[24:15], func3, Instruction_S1[11:0]}));  // open: en, clr
  Multiplexer #(.width(32)) multiplexer_2 (.in0(Instruction), .in1(32'h13), .out(multiplexer_2_out), .sel(PCSel));
  Register #(.width(32)) register_2 (.D(ProgramCounter), .clk(clk), .Q(PC_S1));  // open: en, clr
  Register #(.width(32)) register_3 (.D(PCplus4), .clk(clk), .Q(PCplus4_S1));  // open: en, clr
  // Probe on RegWEn
  regfile regfile_1 (
    .ReadIndex1(Instruction_S1[19:15]), .ReadIndex2(Instruction_S1[24:20]),
    .WriteIndex(Instruction_S1[11:7]), .WriteData(WriteBack), .RegWEn(RegWEn), .clk(clk), .ra(ra), .sp(sp),
    .t0(t0), .t1(t1), .t2(t2), .s0(s0), .s1(s1), .a0(a0), .ReadData1(RegData1), .ReadData2(RegData2));
  imm_gen imm_gen_1 (
    .Instruction({func7, Instruction_S1[24:15], func3, Instruction_S1[11:0]}), .ImmSel(ImmSel),
    .Immediate(IMM));
  control_logic control_logic_1 (
    .Instruction({func7, Instruction_S1[24:15], func3, Instruction_S1[11:0]}), .BrEq(BrEq), .BrLt(BrLt),
    .PCSel(PCSel), .RegWEn(RegWEn), .ImmSel(ImmSel), .BrUn(BrUn), .ASel(ASel), .BSel(BSel), .ALUSel(ALUSel),
    .MemWEn(MemRW), .WBSel(WBSel));
  // Probe on multiplexer_4_out
  // Probe on multiplexer_3_out
  Multiplexer #(.width(32)) multiplexer_3 (.in0(PC_S1), .in1(RegData1), .out(multiplexer_3_out), .sel(ASel));
  Multiplexer #(.width(32)) multiplexer_4 (.in0(IMM), .in1(RegData2), .out(multiplexer_4_out), .sel(BSel));
  // Probe on MemAddress
  alu alu_1 (.A(multiplexer_3_out), .B(multiplexer_4_out), .ALUSel(ALUSel), .ALUResult(MemAddress));
  branch_comp branch_comp_1 (.BrData1(RegData1), .BrData2(RegData2), .BrUn(BrUn), .BrEq(BrEq), .BrLt(BrLt));
  // Probe on MemReadData
  partial_store partial_store_1 (
    .Instruction({func7, Instruction_S1[24:15], func3, Instruction_S1[11:0]}), .MemAddress(MemAddress),
    .DataFromReg(RegData2), .MemRW(MemRW), .MemWriteMask(MemWriteMask), .DataToMem(MemWriteData));
  // Probe on MemWriteData
  partial_load partial_load_1 (
    .Instruction({func7, Instruction_S1[24:15], func3, Instruction_S1[11:0]}), .MemAddress(MemAddress),
    .DataFromMem(MemReadData), .DataToReg(DataToReg));
  // Probe on DataToReg
  Multiplexer #(.select(2), .width(32)) multiplexer_5 (
    .in0(DataToReg), .in1(MemAddress), .in2(PCplus4_S1), .out(WriteBack), .sel(WBSel));  // open: in3
  // Probe on WBSel

  // Other names for the same wires on the sheet: ALUResult[31:0] = MemAddress; opcode[6:0] = Instruction_S1[6:0];
  //   RD[4:0] = Instruction_S1[11:7]; Instruction_S1 (some bits) = {func7, func3}; RS1[4:0] = Instruction_S1[19:15];
  //   RS2[4:0] = Instruction_S1[24:20]

  // Notes on the sheet:
  //   IF
  //   To IMEM
  //   IMEM (do **NOT** move this)
  //   From IMEM
  //   Inputs/Outputs for testing. Do **NOT** move these.
  //   It is OK to move the PC, RegFile, ALU, MEM, Branch Comp, Imm Gen, Partial Load, Partial Store and Control Logic to wherever is most convenient for you when constructing your CPU, and to delete this text
  //   ID
  //   EX
  //   To DMEM
  //   DMEM (do **NOT** move this)
  //   MEM
  //   From DMEM
endmodule
