// Logisim project regfile.circ as structural Verilog: 1 circuit, main circuit regfile
module regfile (
  input  [4:0] ReadIndex1,
  input  [4:0] ReadIndex2,
  input  [4:0] WriteIndex,
  input  [31:0] WriteData,
  input  RegWEn,
  input  clk,
  output [31:0] ra,
  output [31:0] sp,
  output [31:0] t0,
  output [31:0] t1,
  output [31:0] t2,
  output [31:0] s0,
  output [31:0] s1,
  output [31:0] a0,
  output [31:0] ReadData1,
  output [31:0] ReadData2
);

  wire X1WE, X2WE, X3WE, X4WE, X5WE, X6WE, X7WE, X8WE, X9WE, X10WE, X11WE, X12WE, X13WE, X14WE, X15WE, X16WE,
       X17WE, X18WE, X19WE, X20WE, X21WE, X22WE, X23WE, X24WE, X25WE, X26WE, X27WE, X28WE, X29WE, X30WE,
       X31WE;
  wire [31:0] X3Q, X4Q, X11Q, X12Q, X13Q, X14Q, X15Q, X16Q, X17Q, X18Q, X19Q, X20Q, X21Q, X22Q, X23Q, X24Q,
       X25Q, X26Q, X27Q, X28Q, X29Q, X30Q, X31Q;

  Demultiplexer #(.select(5)) demultiplexer_1 (
    .out1(X1WE), .out2(X2WE), .out3(X3WE), .out4(X4WE), .out5(X5WE), .out6(X6WE), .out7(X7WE), .out8(X8WE),
    .out9(X9WE), .out10(X10WE), .out11(X11WE), .out12(X12WE), .out13(X13WE), .out14(X14WE), .out15(X15WE),
    .out16(X16WE), .out17(X17WE), .out18(X18WE), .out19(X19WE), .out20(X20WE), .out21(X21WE), .out22(X22WE),
    .out23(X23WE), .out24(X24WE), .out25(X25WE), .out26(X26WE), .out27(X27WE), .out28(X28WE), .out29(X29WE),
    .out30(X30WE), .out31(X31WE), .in(RegWEn), .sel(WriteIndex));  // open: out0
  Register #(.width(32)) register_1 (.D(WriteData), .en(X3WE), .clk(clk), .Q(X3Q));  // open: clr
  Register #(.width(32)) register_2 (.D(WriteData), .en(X6WE), .clk(clk), .Q(t1));  // open: clr
  Register #(.width(32)) register_3 (.D(WriteData), .en(X9WE), .clk(clk), .Q(s1));  // open: clr
  Register #(.width(32)) register_4 (.D(WriteData), .en(X12WE), .clk(clk), .Q(X12Q));  // open: clr
  Register #(.width(32)) register_5 (.D(WriteData), .en(X15WE), .clk(clk), .Q(X15Q));  // open: clr
  Register #(.width(32)) register_6 (.D(WriteData), .en(X18WE), .clk(clk), .Q(X18Q));  // open: clr
  Register #(.width(32)) register_7 (.D(WriteData), .en(X21WE), .clk(clk), .Q(X21Q));  // open: clr
  Register #(.width(32)) register_8 (.D(WriteData), .en(X24WE), .clk(clk), .Q(X24Q));  // open: clr
  Register #(.width(32)) register_9 (.D(WriteData), .en(X27WE), .clk(clk), .Q(X27Q));  // open: clr
  Register #(.width(32)) register_10 (.D(WriteData), .en(X30WE), .clk(clk), .Q(X30Q));  // open: clr
  Register #(.width(32)) register_11 (.D(WriteData), .en(X1WE), .clk(clk), .Q(ra));  // open: clr
  Register #(.width(32)) register_12 (.D(WriteData), .en(X4WE), .clk(clk), .Q(X4Q));  // open: clr
  Register #(.width(32)) register_13 (.D(WriteData), .en(X7WE), .clk(clk), .Q(t2));  // open: clr
  Register #(.width(32)) register_14 (.D(WriteData), .en(X10WE), .clk(clk), .Q(a0));  // open: clr
  Register #(.width(32)) register_15 (.D(WriteData), .en(X13WE), .clk(clk), .Q(X13Q));  // open: clr
  Register #(.width(32)) register_16 (.D(WriteData), .en(X16WE), .clk(clk), .Q(X16Q));  // open: clr
  Register #(.width(32)) register_17 (.D(WriteData), .en(X19WE), .clk(clk), .Q(X19Q));  // open: clr
  Register #(.width(32)) register_18 (.D(WriteData), .en(X22WE), .clk(clk), .Q(X22Q));  // open: clr
  Register #(.width(32)) register_19 (.D(WriteData), .en(X25WE), .clk(clk), .Q(X25Q));  // open: clr
  Register #(.width(32)) register_20 (.D(WriteData), .en(X28WE), .clk(clk), .Q(X28Q));  // open: clr
  Register #(.width(32)) register_21 (.D(WriteData), .en(X31WE), .clk(clk), .Q(X31Q));  // open: clr
  Register #(.width(32)) register_22 (.D(WriteData), .en(X2WE), .clk(clk), .Q(sp));  // open: clr
  Register #(.width(32)) register_23 (.D(WriteData), .en(X5WE), .clk(clk), .Q(t0));  // open: clr
  Register #(.width(32)) register_24 (.D(WriteData), .en(X8WE), .clk(clk), .Q(s0));  // open: clr
  Register #(.width(32)) register_25 (.D(WriteData), .en(X11WE), .clk(clk), .Q(X11Q));  // open: clr
  Register #(.width(32)) register_26 (.D(WriteData), .en(X14WE), .clk(clk), .Q(X14Q));  // open: clr
  Register #(.width(32)) register_27 (.D(WriteData), .en(X17WE), .clk(clk), .Q(X17Q));  // open: clr
  Register #(.width(32)) register_28 (.D(WriteData), .en(X20WE), .clk(clk), .Q(X20Q));  // open: clr
  Register #(.width(32)) register_29 (.D(WriteData), .en(X23WE), .clk(clk), .Q(X23Q));  // open: clr
  Register #(.width(32)) register_30 (.D(WriteData), .en(X26WE), .clk(clk), .Q(X26Q));  // open: clr
  Register #(.width(32)) register_31 (.D(WriteData), .en(X29WE), .clk(clk), .Q(X29Q));  // open: clr
  Multiplexer #(.select(5), .width(32)) multiplexer_1 (
    .in0({32{1'b0}}), .in1(ra), .in2(sp), .in3(X3Q), .in4(X4Q), .in5(t0), .in6(t1), .in7(t2), .in8(s0),
    .in9(s1), .in10(a0), .in11(X11Q), .in12(X12Q), .in13(X13Q), .in14(X14Q), .in15(X15Q), .in16(X16Q),
    .in17(X17Q), .in18(X18Q), .in19(X19Q), .in20(X20Q), .in21(X21Q), .in22(X22Q), .in23(X23Q), .in24(X24Q),
    .in25(X25Q), .in26(X26Q), .in27(X27Q), .in28(X28Q), .in29(X29Q), .in30(X30Q), .in31(X31Q),
    .out(ReadData1), .sel(ReadIndex1));
  Multiplexer #(.select(5), .width(32)) multiplexer_2 (
    .in0({32{1'b0}}), .in1(ra), .in2(sp), .in3(X3Q), .in4(X4Q), .in5(t0), .in6(t1), .in7(t2), .in8(s0),
    .in9(s1), .in10(a0), .in11(X11Q), .in12(X12Q), .in13(X13Q), .in14(X14Q), .in15(X15Q), .in16(X16Q),
    .in17(X17Q), .in18(X18Q), .in19(X19Q), .in20(X20Q), .in21(X21Q), .in22(X22Q), .in23(X23Q), .in24(X24Q),
    .in25(X25Q), .in26(X26Q), .in27(X27Q), .in28(X28Q), .in29(X29Q), .in30(X30Q), .in31(X31Q),
    .out(ReadData2), .sel(ReadIndex2));

  // Other names for the same wires on the sheet: X1Q[31:0] = ra; X2Q[31:0] = sp; X5Q[31:0] = t0; X6Q[31:0] = t1;
  //   X7Q[31:0] = t2; X8Q[31:0] = s0; X1D[31:0] = WriteData; X2D[31:0] = WriteData; X3D[31:0] = WriteData;
  //   X4D[31:0] = WriteData; X5D[31:0] = WriteData; X6D[31:0] = WriteData; X7D[31:0] = WriteData;
  //   X8D[31:0] = WriteData; X9D[31:0] = WriteData; X10D[31:0] = WriteData; X11D[31:0] = WriteData;
  //   X12D[31:0] = WriteData; X13D[31:0] = WriteData; X14D[31:0] = WriteData; X15D[31:0] = WriteData;
  //   X16D[31:0] = WriteData; X17D[31:0] = WriteData; X18D[31:0] = WriteData; X19D[31:0] = WriteData;
  //   X20D[31:0] = WriteData; X21D[31:0] = WriteData; X22D[31:0] = WriteData; X23D[31:0] = WriteData;
  //   X24D[31:0] = WriteData; X25D[31:0] = WriteData; X26D[31:0] = WriteData; X27D[31:0] = WriteData;
  //   X28D[31:0] = WriteData; X29D[31:0] = WriteData; X30D[31:0] = WriteData; X31D[31:0] = WriteData; X9Q[31:0] = s1;
  //   X10Q[31:0] = a0

  // Notes on the sheet:
  //   INPUTS to your circuit
  //   DON'T CHANGE THE LOCATIONS OF THE INPUTS AND OUTPUTS!
  //   These are DEBUG/TEST outputs from your circuit.
  //   OUTPUTS from your circuit
endmodule
